// Logisim project CPU_Design.circ as structural Verilog: 4 circuits, main circuit Register_File
module Register_File (
  input  [3:0] RS,
  input  register_write,
  input  [3:0] RT,
  input  [3:0] RD,
  input  in_5,
  input  [23:0] Data_input,
  output [23:0] RS_Out,
  output [23:0] RT_Out
);

  wire demultiplexer_1_out0, demultiplexer_1_out1, demultiplexer_1_out2, demultiplexer_1_out3,
       demultiplexer_1_out4, demultiplexer_1_out5, demultiplexer_1_out6, demultiplexer_1_out7,
       demultiplexer_1_out8, demultiplexer_1_out9, demultiplexer_1_out10, demultiplexer_1_out11,
       demultiplexer_1_out12, demultiplexer_1_out13, demultiplexer_1_out14, demultiplexer_1_out15, undriven;
  wire [23:0] Reg1_q, Reg2_q, Reg3_q, Reg4_q, Reg5_q, Reg6_q, Reg7_q, Reg8_q, Reg9_q, Reg10_q, Reg11_q,
       Reg12_q, Reg13_q, Reg14_q, Reg15_q, Reg16_q;

  Demultiplexer #(.select(4)) demultiplexer_1 (
    .out0(demultiplexer_1_out0), .out1(demultiplexer_1_out1), .out2(demultiplexer_1_out2),
    .out3(demultiplexer_1_out3), .out4(demultiplexer_1_out4), .out5(demultiplexer_1_out5),
    .out6(demultiplexer_1_out6), .out7(demultiplexer_1_out7), .out8(demultiplexer_1_out8),
    .out9(demultiplexer_1_out9), .out10(demultiplexer_1_out10), .out11(demultiplexer_1_out11),
    .out12(demultiplexer_1_out12), .out13(demultiplexer_1_out13), .out14(demultiplexer_1_out14),
    .out15(demultiplexer_1_out15), .in(register_write), .sel(RD));  // open: en
  Register #(.width(24)) Reg1 (.D(Data_input), .en(demultiplexer_1_out0), .Q(Reg1_q), .clk(undriven));  // open: clr
  Register #(.width(24)) Reg2 (.D(Data_input), .en(demultiplexer_1_out1), .Q(Reg2_q), .clk(undriven));  // open: clr
  Register #(.width(24)) Reg3 (.D(Data_input), .en(demultiplexer_1_out2), .Q(Reg3_q), .clk(undriven));  // open: clr
  Register #(.width(24)) Reg4 (.D(Data_input), .en(demultiplexer_1_out3), .Q(Reg4_q), .clk(undriven));  // open: clr
  Register #(.width(24)) Reg5 (.D(Data_input), .en(demultiplexer_1_out4), .Q(Reg5_q), .clk(undriven));  // open: clr
  Register #(.width(24)) Reg6 (.D(Data_input), .en(demultiplexer_1_out5), .Q(Reg6_q), .clk(undriven));  // open: clr
  Register #(.width(24)) Reg7 (.D(Data_input), .en(demultiplexer_1_out6), .Q(Reg7_q), .clk(undriven));  // open: clr
  Register #(.width(24)) Reg8 (.D(Data_input), .en(demultiplexer_1_out7), .Q(Reg8_q), .clk(undriven));  // open: clr
  Register #(.width(24)) Reg9 (.D(Data_input), .en(demultiplexer_1_out8), .Q(Reg9_q), .clk(undriven));  // open: clr
  Register #(.width(24)) Reg10 (.D(Data_input), .en(demultiplexer_1_out9), .Q(Reg10_q), .clk(undriven));  // open: clr
  Register #(.width(24)) Reg11 (.D(Data_input), .en(demultiplexer_1_out10), .Q(Reg11_q), .clk(undriven));  // open: clr
  Register #(.width(24)) Reg12 (.D(Data_input), .en(demultiplexer_1_out11), .Q(Reg12_q), .clk(undriven));  // open: clr
  Register #(.width(24)) Reg13 (.D(Data_input), .en(demultiplexer_1_out12), .Q(Reg13_q), .clk(undriven));  // open: clr
  Register #(.width(24)) Reg14 (.D(Data_input), .en(demultiplexer_1_out13), .Q(Reg14_q), .clk(undriven));  // open: clr
  Register #(.width(24)) Reg15 (.D(Data_input), .en(demultiplexer_1_out14), .Q(Reg15_q), .clk(undriven));  // open: clr
  Register #(.width(24)) Reg16 (.D(Data_input), .en(demultiplexer_1_out15), .Q(Reg16_q), .clk(undriven));  // open: clr
  Multiplexer #(.select(4), .width(24), .enable("false")) multiplexer_1 (
    .in0(Reg1_q), .in1(Reg2_q), .in2(Reg3_q), .in3(Reg4_q), .in4(Reg5_q), .in5(Reg6_q), .in6(Reg7_q),
    .in7(Reg8_q), .in8(Reg9_q), .in9(Reg10_q), .in10(Reg11_q), .in11(Reg12_q), .in12(Reg13_q),
    .in13(Reg14_q), .in14(Reg15_q), .in15(Reg16_q), .out(RS_Out), .sel(RS));
  Multiplexer #(.select(4), .width(24), .enable("false")) multiplexer_2 (
    .in0(Reg1_q), .in1(Reg2_q), .in2(Reg3_q), .in3(Reg4_q), .in4(Reg5_q), .in5(Reg6_q), .in6(Reg7_q),
    .in7(Reg8_q), .in8(Reg9_q), .in9(Reg10_q), .in10(Reg11_q), .in11(Reg12_q), .in12(Reg13_q),
    .in13(Reg14_q), .in14(Reg15_q), .in15(Reg16_q), .out(RT_Out), .sel(RT));
endmodule

module ALU (
  input  [23:0] in_1,
  input  [23:0] in_2,
  input  [2:0] ALUctr,
  output [23:0] ALU_Output,
  output greater,
  output equal
);

  wire [23:0] adder_1_out, and_1_out, divider_1_out, multiplier_1_out, or_1_out, shifter_1_out,
       shifter_2_out, subtractor_1_out;

  assign and_1_out = in_1 & in_2;  // AND_Gate and_1, 24 bits wide
  assign or_1_out = in_1 | in_2;  // OR_Gate or_1, 24 bits wide
  Adder #(.width(24)) adder_1 (.a(in_1), .b(in_2), .out(adder_1_out));  // open: cin, cout
  Subtractor #(.width(24)) subtractor_1 (.a(in_1), .b(in_2), .out(subtractor_1_out));  // open: bin, bout
  Multiplier #(.width(24)) multiplier_1 (.a(in_1), .b(in_2), .out(multiplier_1_out));  // open: cin, cout
  Divider #(.width(24)) divider_1 (.a(in_1), .b(in_2), .out(divider_1_out));  // open: upper, rem
  Shifter #(.width(24)) shifter_1 (.in(in_1), .\dist (in_2[4:0]), .out(shifter_1_out));
  Shifter #(.width(24), .shift("ar")) shifter_2 (.in(in_1), .\dist (in_2[4:0]), .out(shifter_2_out));
  Multiplexer #(.select(3), .width(24), .enable("false")) multiplexer_1 (
    .in0(and_1_out), .in1(or_1_out), .in2(adder_1_out), .in3(subtractor_1_out), .in4(multiplier_1_out),
    .in5(divider_1_out), .in6(shifter_1_out), .in7(shifter_2_out), .out(ALU_Output), .sel(ALUctr));
  Comparator #(.width(24)) comparator_1 (.a(ALU_Output), .b({24{1'b0}}), .gt(greater), .eq(equal));  // open: lt
endmodule

module Control_Unit (
  input  [5:0] OpCode,
  output RegDst,
  output ALUSrc,
  output MemtoReg,
  output RegWrite,
  output MemWrite,
  output MemRead,
  output Branch_Eq,
  output Branch_Gr,
  output Jump,
  output ExtOp,
  output [2:0] ALUOp
);

  wire addi_out, andi_out, ori_out;

  and R_Type (ALUOp[2], ~OpCode[5], ~OpCode[4], ~OpCode[3], ~OpCode[2], ~OpCode[1], ~OpCode[0]);  // AND_Gate
  and addi (addi_out, ~OpCode[5], ~OpCode[4], ~OpCode[3], ~OpCode[2], ~OpCode[1], OpCode[0]);  // AND_Gate
  and ori (ori_out, ~OpCode[5], ~OpCode[4], ~OpCode[3], ~OpCode[2], OpCode[1], ~OpCode[0]);  // AND_Gate
  and andi (andi_out, ~OpCode[5], ~OpCode[4], ~OpCode[3], ~OpCode[2], OpCode[1], OpCode[0]);  // AND_Gate
  and lw (MemRead, ~OpCode[5], ~OpCode[4], ~OpCode[3], OpCode[2], ~OpCode[1], ~OpCode[0]);  // AND_Gate
  and sw (MemWrite, ~OpCode[5], ~OpCode[4], ~OpCode[3], OpCode[2], ~OpCode[1], OpCode[0]);  // AND_Gate
  and beq (Branch_Eq, ~OpCode[5], ~OpCode[4], ~OpCode[3], OpCode[2], OpCode[1], ~OpCode[0]);  // AND_Gate
  and bgt (Branch_Gr, ~OpCode[5], ~OpCode[4], ~OpCode[3], OpCode[2], OpCode[1], OpCode[0]);  // AND_Gate
  or or_1 (ALUSrc, MemWrite, addi_out, ori_out, andi_out, MemRead);
  or or_2 (RegWrite, ALUOp[2], addi_out, ori_out, andi_out, MemRead);
  and u_jump (Jump, ~OpCode[5], ~OpCode[4], OpCode[3], ~OpCode[2], ~OpCode[1], ~OpCode[0]);  // AND_Gate
  or or_3 (ExtOp, MemRead, MemWrite, Branch_Eq, Branch_Gr);
  or or_4 (ALUOp[0], ori_out, Branch_Eq, Branch_Gr);
  or or_5 (ALUOp[1], addi_out, MemRead, MemWrite, Branch_Eq, Branch_Gr);

  assign MemtoReg = MemRead;
  assign RegDst = ALUOp[2];
endmodule

module Alu_Control (
  input  [5:0] \function ,
  input  [2:0] ALUOp,
  output [2:0] ALUctr
);

  wire [2:0] and_1_out;

  and and_1 (and_1_out[0], \function [2], ~\function [3], ~\function [4], ~\function [5]);  // AND_Gate
  and and_2 (and_1_out[1], \function [0], ~\function [3], ~\function [4], ~\function [5]);  // AND_Gate
  and and_3 (and_1_out[2], \function [1], ~\function [3], ~\function [4], ~\function [5]);  // AND_Gate
  Multiplexer #(.width(3), .enable("false")) multiplexer_1 (.in0(ALUOp), .in1(and_1_out), .out(ALUctr), .sel(ALUOp[2]));

  // Notes on the sheet:
  //   operation 2
  //   operation 0
  //   operation 1
endmodule
